# Fritzing sketch go-light (saved by Fritzing 0.9.3b)
stripboards: 1

parts:
  IC1 = ULN2803A [package=THT]
  J8 = male pin header, 8 pins [form="♂ (male)"]
  U1 = NodeMCU V3.0

nets:
  N1: IC1.In_2, IC1.In_5, IC1.0V, J8.pin3, J8.pin6, U1.GND#6, U1.D7, U1.GND#13, U1.GND#16, U1.GND#33, U1.SC
  N2: IC1.In_3, J8.pin4, U1.D5, U1.S0
  N3: IC1.In_4, U1.D6, U1.SK
  3V3: IC1.In_6, J8.pin2, U1.3V3, U1.D8, U1.Vin, U1.S1
  N4: IC1.In_7, U1.D1, U1.GND#41
  N5: IC1.In_8, J8.pin1, U1.D2, U1.VU
  N6: IC1.Out_2, J8.pin7
  N7: J8.pin8, U1.D3, U1.S3
  N8: U1.D0, U1.A0
  N9: U1.D4, U1.S2
  N10: U1.RX, U1.EN
  N11: U1.TX, U1.RST

custom parts:
  NodeMCU V3.0: ESP8266 based NodeMCU
